# Fritzing sketch maquette (saved by Fritzing 0.8.3b)
breadboards: 1

parts:
  Composants1 = Arduino Mega 2560 (Rev3)
  S2 = Pushbutton [package=THT]
  C1 = Ceramic Capacitor [capacitance=100nF package="100 mil [THT, multilayer]"]
  R1 = Resistor [tolerance=±5% resistance=220 package=THT]
  S3 = Pushbutton [package=THT]
  C2 = Ceramic Capacitor [capacitance=100nF package="100 mil [THT, multilayer]"]
  R2 = Resistor [tolerance=±5% resistance=220 package=THT]
  S4 = Pushbutton [package=THT]
  C3 = Ceramic Capacitor [capacitance=100nF package="100 mil [THT, multilayer]"]
  R3 = Resistor [tolerance=±5% resistance=220 package=THT]
  LED1 = LED - 5mm [color="Red (633nm)" package="5 mm [THT]"]
  R4 = Resistor [tolerance=±5% resistance=220 package=THT]
  LED2 = LED - 5mm [color="Red (633nm)" package="5 mm [THT]"]
  R5 = Resistor [tolerance=±5% resistance=220 package=THT]
  LED3 = LED - 5mm [color="Red (633nm)" package="5 mm [THT]"]
  R6 = Resistor [tolerance=±5% resistance=220 package=THT]
  S6 = Pushbutton [package=THT]
  C4 = Ceramic Capacitor [capacitance=100nF package="100 mil [THT, multilayer]"]
  R7 = Resistor [tolerance=±5% resistance=220 package=THT]

nets:
  N1: Composants1.D20/SDA, S2.leg1, C1.1, R1.Pin_1
  N2: Composants1.D19/RX1, S3.leg1, C2.1, R2.Pin_1
  N3: Composants1.5V, R1.Pin_0, R2.Pin_0, R3.Pin_0, R7.Pin_0
  N4: Composants1.GND, S2.leg0, C1.0, S4.leg0, C3.0, LED1.cathode, LED2.cathode, LED3.cathode
  N5: Composants1.D2_PWM, S4.leg1, C3.1, R3.Pin_1
  N6: Composants1.D3_PWM, S6.leg1, C4.1, R7.Pin_1
  N7: Composants1.D4_PWM, R4.Pin_0
  N8: Composants1.D5_PWM, R5.Pin_0
  N9: Composants1.D6_PWM, R6.Pin_0
  N10: S3.leg0, C2.0
  N11: LED1.anode, R4.Pin_1
  N12: LED2.anode, R5.Pin_1
  N13: LED3.anode, R6.Pin_1
  N14: S6.leg0, C4.0
